// Logisim project Dekompozycja1.circ as structural Verilog: 1 circuit, main circuit main
module main (
  input  [5:0] x5x4x3x2x1x0,
  output [1:0] y1y0
);

  wire g;

  ROM #(.addrWidth(3), .dataWidth(1)) rom_1 (.addr(x5x4x3x2x1x0[5:3]), .data(g));  // open: sel
  ROM #(.addrWidth(4), .dataWidth(2)) rom_2 (.addr({x5x4x3x2x1x0[2:0], g}), .data(y1y0));  // open: sel

  // Other names for the same wires on the sheet: x0 = x5x4x3x2x1x0[0]; x1 = x5x4x3x2x1x0[1]; x2 = x5x4x3x2x1x0[2];
  //   x3 = x5x4x3x2x1x0[3]; x4 = x5x4x3x2x1x0[4]; x5 = x5x4x3x2x1x0[5]

  // Notes on the sheet:
  //   Funkcja G
  //   Funkcja H
  //   contents of rom_1 (hex, n*v repeats v):
  //   0 1 4*0 1
  //   contents of rom_2 (hex, n*v repeats v):
  //   5*0 3 0 3 0 2 0 0 1 2 2 1
endmodule
